// Digital circuit Controller.dig as structural Verilog
module Controller (
  input  [3:0] From_IR,
  input  Pulse,
  input  R_CLK,
  output CLK,
  output CLR,
  output O_pc,
  output L_a,
  output O_a,
  output L_m,
  output S_u,
  output O_u,
  output S_mem,
  output O_mem,
  output L_ram,
  output L_b,
  output L_i,
  output O_i,
  output L_o,
  output Inc,
  output Gt,
  output eq,
  output Lt,
  output Is_Running,
  output Halt
);

  wire nor_1_out, not_2_out, or_1_out;
  wire [2:0] ring_counter_1_t_n;
  wire [7:0] add_1_s, bitextender_1_out, lookuptable_1_out;
  wire [14:5] rom_1_d;

  not not_1 (Is_Running, Halt);
  or or_1 (or_1_out, R_CLK, Pulse);
  Comparator #(.Bits(4)) comparator_1 (.a(From_IR), .b(4'b1001), .eq(Halt));  // open: gt, lt
  not not_2 (not_2_out, Halt);
  and and_1 (CLK, not_2_out, or_1_out);
  Ring_Counter ring_counter_1 (
    .CLK(CLK), .CLR(rom_1_d[14]), .T_1(O_pc), .T_2(Inc), .T_3(L_i), .T_n(ring_counter_1_t_n));
  LookUpTable #(.Bits(8)) lookuptable_1 (
    .in0(From_IR[0]), .in1(From_IR[1]), .in2(From_IR[2]), .in3(From_IR[3]), .out(lookuptable_1_out));
  BitExtender #(.inputBits(3), .outputBits(8)) bitextender_1 (.in(ring_counter_1_t_n), .out(bitextender_1_out));
  nor nor_1 (nor_1_out, L_i, Inc, O_pc);
  // Probe on lookuptable_1_out
  Add #(.Bits(8)) add_1 (.a(lookuptable_1_out), .b(bitextender_1_out), .c_i(1'b0), .s(add_1_s));  // open: c_o
  PullDown pulldown_1 (.out(CLR));
  // Probe on {rom_1_d[14:13], Lt, eq, Gt, L_o, O_i, L_b, L_ram, rom_1_d[5], S_mem, O_u, S_u, O_a, L_a}
  ROM #(.AddrBits(8), .Bits(15)) rom_1 (
    .A(add_1_s), .sel(nor_1_out),
    .D({rom_1_d[14:13], Lt, eq, Gt, L_o, O_i, L_b, L_ram, rom_1_d[5], S_mem, O_u, S_u, O_a, L_a}));
  PullDown pulldown_2 (.out(rom_1_d[14]));
  PullDown pulldown_3 (.out(L_a));
  PullDown pulldown_4 (.out(O_a));
  PullDown pulldown_5 (.out(rom_1_d[13]));
  PullDown pulldown_6 (.out(S_u));
  PullDown pulldown_7 (.out(O_u));
  PullDown pulldown_8 (.out(S_mem));
  PullDown pulldown_9 (.out(rom_1_d[5]));
  PullDown pulldown_10 (.out(L_ram));
  PullDown pulldown_11 (.out(L_b));
  PullDown pulldown_12 (.out(O_i));
  PullDown pulldown_13 (.out(L_o));
  PullDown pulldown_14 (.out(Gt));
  or or_2 (L_m, rom_1_d[13], O_pc);
  PullDown pulldown_15 (.out(eq));
  PullDown pulldown_16 (.out(Lt));
  or or_3 (O_mem, rom_1_d[5], L_i);

  // Notes on the sheet:
  //   contents of lookuptable_1 (hex, n*v repeats v):
  //   0,5,a,f,14,19,1e,23,28,2d,32,37,3c,41
  //   contents of rom_1 (hex, n*v repeats v):
  //   5*0,101,4000,0,0,0,180,4000,0,0,0,2100,52,4000,0,0,2100,31,4000
  //   ,0,0,2100,b0,4000,0,0,9,4000,0,0,0,d,4000,0,0,0,202,9*0,1d00,4000
  //   ,0,0,0,900,4000,0,0,0,1100,4000,0,0,0,500,4000
endmodule
