// Digital circuit Hex-to-dec-display.dig as structural Verilog
module Hex_to_dec_display (
  input  [7:0] in,
  output [3:0] b1,
  output [3:0] c1,
  output [3:0] a1,
  output [2:0] a2,
  output [2:0] b2,
  output [2:0] c2
);

  ROM #(.AddrBits(8), .Bits(7)) rom_1 (.A(in), .sel(1'b1), .D({a1, a2}));
  ROM #(.AddrBits(8), .Bits(7)) rom_2 (.A(in), .sel(1'b1), .D({b1, b2}));
  ROM #(.AddrBits(8), .Bits(7)) rom_3 (.A(in), .sel(1'b1), .D({c1, c2}));

  // Notes on the sheet:
  //   contents of rom_1 (hex, n*v repeats v):
  //   100*7e,100*30,56*6d
  //   contents of rom_2 (hex, n*v repeats v):
  //   10*7e,10*30,10*6d,10*79,10*33,10*5b,10*5f,10*70,10*7f,10*7b,10*7e
  //   ,10*30,10*6d,10*79,10*33,10*5b,10*5f,10*70,10*7f,10*7b,10*7e,10*30
  //   ,10*6d,10*79,10*33,6*5b
  //   contents of rom_3 (hex, n*v repeats v):
  //   7e,30,6d,79,33,5b,5f,70,7f,7b,7e,30,6d,79,33,5b,5f,70,7f,7b,7e
  //   ,30,6d,79,33,5b,5f,70,7f,7b,7e,30,6d,79,33,5b,5f,70,7f,7b,7e,30
  //   ,6d,79,33,5b,5f,70,7f,7b,7e,30,6d,79,33,5b,5f,70,7f,7b,7e,30,6d
  //   ,79,33,5b,5f,70,7f,7b,7e,30,6d,79,33,5b,5f,70,7f,7b,7e,30,6d,79
  //   ,33,5b,5f,70,7f,7b,7e,30,6d,79,33,5b,5f,70,7f,7b,7e,30,6d,79,33
  //   ,5b,5f,70,7f,7b,7e,30,6d,79,33,5b,5f,70,7f,7b,7e,30,6d,79,33,5b
  //   ,5f,70,7f,7b,7e,30,6d,79,33,5b,5f,70,7f,7b,7e,30,6d,79,33,5b,5f
  //   ,70,7f,7b,7e,30,6d,79,33,5b,5f,70,7f,7b,7e,30,6d,79,33,5b,5f,70
  //   ,7f,7b,7e,30,6d,79,33,5b,5f,70,7f,7b,7e,30,6d,79,33,5b,5f,70,7f
  //   ,7b,7e,30,6d,79,33,5b,5f,70,7f,7b,7e,30,6d,79,33,5b,5f,70,7f,7b
  //   ,7e,30,6d,79,33,5b,5f,70,7f,7b,7e,30,6d,79,33,5b,5f,70,7f,7b,7e
  //   ,30,6d,79,33,5b,5f,70,7f,7b,7e,30,6d,79,33,5b,5f,70,7f,7b,7e,30
  //   ,6d,79,33,5b
endmodule
