// Digital circuit main.dig as structural Verilog
module main (
  input  clk
);

  wire accumulator_1_p3, alu_1_p3, alu_1_p4, alu_1_p5, alu_1_p6, and_1_out, CLK_t, CLR, controller_1_halt,
       controller_1_is_running, dipswitch_1_out, eq, gt, Inc, j, L_a, L_b, L_i, L_m, L_o, L_RAM, lt, O_a,
       O_i, O_mem, O_pc, O_u, Pulse_out, S_mem, S_u;
  wire [2:0] hex_to_dec_display_1_a2, hex_to_dec_display_1_b2, hex_to_dec_display_1_c2;
  wire [3:0] hex_to_dec_display_1_a1, hex_to_dec_display_1_b1, hex_to_dec_display_1_c1,
       instruction_register_1_to_controller;
  wire [7:0] mar_1_to_mem, output_register_1_to_display, program_counter_1_w_out;

  DipSwitch dipswitch_1 (.out(dipswitch_1_out));
  LED Running (.in(controller_1_is_running));
  LED Halt (.in(controller_1_halt));
  and and_1 (and_1_out, clk, dipswitch_1_out);
  Controller controller_1 (
    .From_IR(instruction_register_1_to_controller), .CLK(CLK_t), .CLR(CLR), .O_pc(O_pc), .Inc(Inc),
    .L_a(L_a), .O_a(O_a), .L_m(L_m), .S_u(S_u), .O_u(O_u), .S_mem(S_mem), .O_mem(O_mem), .L_ram(L_RAM),
    .L_b(L_b), .L_i(L_i), .O_i(O_i), .L_o(L_o), .Gt(gt), .eq(eq), .Lt(lt),
    .Is_Running(controller_1_is_running), .Halt(controller_1_halt), .R_CLK(and_1_out), .Pulse(Pulse_out));
  Button Pulse (.out(Pulse_out));
  Program_Counter program_counter_1 (
    .W_in(program_counter_1_w_out), .W_out(program_counter_1_w_out), .Inc(Inc), .CLK(CLK_t), .j(j),
    .O_pc(O_pc));
  MAR mar_1 (.W_in(program_counter_1_w_out), .CLK(CLK_t), .L_m(L_m), .To_mem(mar_1_to_mem));
  Combined_Memory combined_memory_1 (
    .S_mem(S_mem), .O_mem(O_mem), .L_RAM(L_RAM), .CLK(CLK_t), .From_mar(mar_1_to_mem),
    .W_out(program_counter_1_w_out), .W_in(program_counter_1_w_out));
  Instruction_Register instruction_register_1 (
    .W_in(program_counter_1_w_out), .W_out(program_counter_1_w_out), .CLK(CLK_t), .L_i(L_i), .O_i(O_i),
    .To_controller(instruction_register_1_to_controller));
  // Probe on program_counter_1_w_out
  // Accumulator accumulator_1: pin names not known; wires that end beside it: program_counter_1_w_out, program_counter_1_w_out, accumulator_1_p3, CLK_t, L_a, O_a
  // ALU alu_1: pin names not known; wires that end beside it: program_counter_1_w_out, accumulator_1_p3, alu_1_p3, alu_1_p4, alu_1_p5, alu_1_p6, S_u, O_u
  // B_Register b_register_1: pin names not known; wires that end beside it: program_counter_1_w_out, alu_1_p3, CLK_t, L_b
  Output_Register output_register_1 (
    .W_in(program_counter_1_w_out), .CLK(CLK_t), .L_O(L_o), .To_display(output_register_1_to_display));
  Hex_to_dec_display hex_to_dec_display_1 (
    .in(output_register_1_to_display), .a1(hex_to_dec_display_1_a1), .a2(hex_to_dec_display_1_a2),
    .b1(hex_to_dec_display_1_b1), .b2(hex_to_dec_display_1_b2), .c1(hex_to_dec_display_1_c1),
    .c2(hex_to_dec_display_1_c2));
  Seven_Seg seven_seg_1 (
    .a(hex_to_dec_display_1_a1[3]), .b(hex_to_dec_display_1_a1[2]), .c(hex_to_dec_display_1_a1[1]),
    .d(hex_to_dec_display_1_a1[0]), .e(hex_to_dec_display_1_a2[2]), .f(hex_to_dec_display_1_a2[1]),
    .g(hex_to_dec_display_1_a2[0]), .dp(1'b0));
  Flags flags_1 (.Gt_ALU(alu_1_p4), .Eq_ALU(alu_1_p5), .Lt_ALU(alu_1_p6), .Gt(gt), .Eq(eq), .Lt(lt), .j(j));
  Seven_Seg seven_seg_2 (
    .a(hex_to_dec_display_1_b1[3]), .b(hex_to_dec_display_1_b1[2]), .c(hex_to_dec_display_1_b1[1]),
    .d(hex_to_dec_display_1_b1[0]), .e(hex_to_dec_display_1_b2[2]), .f(hex_to_dec_display_1_b2[1]),
    .g(hex_to_dec_display_1_b2[0]), .dp(1'b0));
  Seven_Seg seven_seg_3 (
    .a(hex_to_dec_display_1_c1[3]), .b(hex_to_dec_display_1_c1[2]), .c(hex_to_dec_display_1_c1[1]),
    .d(hex_to_dec_display_1_c1[0]), .e(hex_to_dec_display_1_c2[2]), .f(hex_to_dec_display_1_c2[1]),
    .g(hex_to_dec_display_1_c2[0]), .dp(1'b0));

  // Notes on the sheet:
  //   clk: Hz: 100
endmodule
